// Logisim project async.circ as structural Verilog: 3 circuits, main circuit asyncCounter
module asyncCounter (
  input  Count,
  input  Clock,
  input  RES,
  output [7:0] dOUT,
  output [7:0] iOUT
);

  J_K_Flip_Flop j_k_ff_1 (
    .J(Count), .clk(Clock), .K(Count), .Q(dOUT[0]), .Qn(iOUT[0]), .reset(RES));  // open: preset, en
  J_K_Flip_Flop j_k_ff_2 (
    .J(Count), .clk(dOUT[0]), .K(Count), .Q(dOUT[1]), .Qn(iOUT[1]), .reset(RES));  // open: preset, en
  J_K_Flip_Flop j_k_ff_3 (
    .J(Count), .clk(dOUT[1]), .K(Count), .Q(dOUT[2]), .Qn(iOUT[2]), .reset(RES));  // open: preset, en
  J_K_Flip_Flop j_k_ff_4 (
    .J(Count), .clk(dOUT[2]), .K(Count), .Q(dOUT[3]), .Qn(iOUT[3]), .reset(RES));  // open: preset, en
  J_K_Flip_Flop j_k_ff_5 (
    .J(Count), .clk(dOUT[3]), .K(Count), .Q(dOUT[4]), .Qn(iOUT[4]), .reset(RES));  // open: preset, en
  J_K_Flip_Flop j_k_ff_6 (
    .J(Count), .clk(dOUT[4]), .K(Count), .Q(dOUT[5]), .Qn(iOUT[5]), .reset(RES));  // open: preset, en
  J_K_Flip_Flop j_k_ff_7 (
    .J(Count), .clk(dOUT[5]), .K(Count), .Q(dOUT[6]), .Qn(iOUT[6]), .reset(RES));  // open: preset, en
  J_K_Flip_Flop j_k_ff_8 (
    .J(Count), .clk(dOUT[6]), .K(Count), .Q(dOUT[7]), .Qn(iOUT[7]), .reset(RES));  // open: preset, en
endmodule

module syncCounter (
  input  CLK,
  input  CNT,
  input  RES,
  output carry,
  output [7:0] iOUT,
  output [7:0] dOUT
);

  wire and_1_out, and_2_out, and_3_out, and_4_out, and_5_out, and_6_out;

  T_Flip_Flop t_ff_1 (.clk(CLK), .T(CNT), .Q(iOUT[0]), .Qn(dOUT[0]), .reset(RES));  // open: preset, en
  and and_1 (and_1_out, iOUT[0], iOUT[1]);
  T_Flip_Flop t_ff_2 (.clk(CLK), .T(iOUT[0]), .Q(iOUT[1]), .Qn(dOUT[1]), .reset(RES));  // open: preset, en
  T_Flip_Flop t_ff_3 (.clk(CLK), .T(and_1_out), .Q(iOUT[2]), .Qn(dOUT[2]), .reset(RES));  // open: preset, en
  and and_2 (and_2_out, and_1_out, iOUT[2]);
  and and_3 (and_3_out, and_2_out, iOUT[3]);
  T_Flip_Flop t_ff_4 (.clk(CLK), .T(and_2_out), .Q(iOUT[3]), .Qn(dOUT[3]), .reset(RES));  // open: preset, en
  T_Flip_Flop t_ff_5 (.clk(CLK), .T(and_3_out), .Q(iOUT[4]), .Qn(dOUT[4]), .reset(RES));  // open: preset, en
  and and_4 (and_4_out, and_3_out, iOUT[4]);
  and and_5 (and_5_out, and_4_out, iOUT[5]);
  T_Flip_Flop t_ff_6 (.clk(CLK), .T(and_4_out), .Q(iOUT[5]), .Qn(dOUT[5]), .reset(RES));  // open: preset, en
  T_Flip_Flop t_ff_7 (.clk(CLK), .T(and_5_out), .Q(iOUT[6]), .Qn(dOUT[6]), .reset(RES));  // open: preset, en
  and and_6 (and_6_out, and_5_out, iOUT[6]);
  and and_7 (carry, and_6_out, iOUT[7]);
  T_Flip_Flop t_ff_8 (.clk(CLK), .T(and_6_out), .Q(iOUT[7]), .Qn(dOUT[7]), .reset(RES));  // open: preset, en
endmodule

module async_load (
  input  [7:0] IMM,
  input  Count,
  input  Load,
  input  Clock,
  input  RES,
  input  DEC,
  output [7:0] OUT,
  output Carry
);

  wire n0, n1, n2, n3, n4, n5, n6, n7, q0, q1, q2, q3, q4, q5, q6, q7, t0, t1, t2, t3, t4, t5, t6, t7, x1,
       x2, x3, x4, x5, x6, xor_1_out, xor_2_out, xor_3_out, xor_4_out, xor_5_out, xor_6_out, xor_7_out,
       xor_8_out;

  J_K_Flip_Flop j_k_ff_1 (.J(t0), .clk(Clock), .K(t0), .Q(q0), .Qn(n0), .reset(RES));  // open: preset, en
  xor xor_1 (xor_1_out, IMM[0], q0);
  Multiplexer multiplexer_1 (.in0(Count), .in1(xor_1_out), .out(t0), .sel(Load));  // open: en
  and and_1 (x4, x3, q3);
  Multiplexer multiplexer_2 (.in0(x4), .in1(xor_2_out), .out(t4), .sel(Load));  // open: en
  xor xor_2 (xor_2_out, IMM[4], q4);
  J_K_Flip_Flop j_k_ff_2 (.J(t1), .clk(Clock), .K(t1), .Q(q1), .Qn(n1), .reset(RES));  // open: preset, en
  and and_2 (x1, Count, q0);
  Multiplexer multiplexer_3 (.in0(x1), .in1(xor_3_out), .out(t1), .sel(Load));  // open: en
  and and_3 (x5, x4, q4);
  Multiplexer multiplexer_4 (.in0(x5), .in1(xor_4_out), .out(t5), .sel(Load));  // open: en
  J_K_Flip_Flop j_k_ff_3 (.J(t2), .clk(Clock), .K(t2), .Q(q2), .Qn(n2), .reset(RES));  // open: preset, en
  xor xor_3 (xor_3_out, IMM[1], q1);
  xor xor_4 (xor_4_out, IMM[5], q5);
  Multiplexer #(.width(8)) multiplexer_5 (
    .in0({q7, q6, q5, q4, q3, q2, q1, q0}), .in1({n7, n6, n5, n4, n3, n2, n1, n0}), .out(OUT), .sel(DEC));  // open: en
  J_K_Flip_Flop j_k_ff_4 (.J(t3), .clk(Clock), .K(t3), .Q(q3), .Qn(n3), .reset(RES));  // open: preset, en
  xor xor_5 (xor_5_out, IMM[2], q2);
  and and_4 (x2, x1, q1);
  Multiplexer multiplexer_6 (.in0(x2), .in1(xor_5_out), .out(t2), .sel(Load));  // open: en
  xor xor_6 (xor_6_out, IMM[6], q6);
  and and_5 (x6, x5, q5);
  Multiplexer multiplexer_7 (.in0(x6), .in1(xor_6_out), .out(t6), .sel(Load));  // open: en
  J_K_Flip_Flop j_k_ff_5 (.J(t4), .clk(Clock), .K(t4), .Q(q4), .Qn(n4), .reset(RES));  // open: preset, en
  and and_6 (x3, x2, q2);
  Multiplexer multiplexer_8 (.in0(x3), .in1(xor_7_out), .out(t3), .sel(Load));  // open: en
  and and_7 (Carry, x6, q6);
  Multiplexer multiplexer_9 (.in0(Carry), .in1(xor_8_out), .out(t7), .sel(Load));  // open: en
  J_K_Flip_Flop j_k_ff_6 (.J(t5), .clk(Clock), .K(t5), .Q(q5), .Qn(n5), .reset(RES));  // open: preset, en
  xor xor_7 (xor_7_out, IMM[3], q3);
  xor xor_8 (xor_8_out, IMM[7], q7);
  J_K_Flip_Flop j_k_ff_7 (.J(t6), .clk(Clock), .K(t6), .Q(q6), .Qn(n6), .reset(RES));  // open: preset, en
  J_K_Flip_Flop j_k_ff_8 (.J(t7), .clk(Clock), .K(t7), .Q(q7), .Qn(n7), .reset(RES));  // open: preset, en

  // Other names for the same wires on the sheet: clk = Clock; cnt = Count; i0 = IMM[0]; i1 = IMM[1]; i2 = IMM[2];
  //   i3 = IMM[3]; i4 = IMM[4]; i5 = IMM[5]; i6 = IMM[6]; i7 = IMM[7]; ld = Load
endmodule
